// Logisim project cpu.circ as structural Verilog
module _10_bit_Register_File (
  input  [9:0] Write_Data,
  input  [1:0] RS,
  input  [1:0] RD,
  input  WE,
  input  in_5,
  input  [1:0] RT,
  output [9:0] Data_1,
  output [9:0] Data_2
);

  wire and_1_out, and_2_out, and_3_out, and_4_out, decoder_1_out0, decoder_1_out1, decoder_1_out2,
       decoder_1_out3;
  wire [9:0] register_1_q, register_2_q, register_3_q, register_4_q;

  Decoder #(.select(2), .enable("false")) decoder_1 (
    .out0(decoder_1_out0), .out1(decoder_1_out1), .out2(decoder_1_out2), .out3(decoder_1_out3), .sel(RD));
  and and_1 (and_1_out, decoder_1_out0, WE);
  and and_2 (and_2_out, decoder_1_out1, WE);
  and and_3 (and_3_out, decoder_1_out2, WE);
  and and_4 (and_4_out, decoder_1_out3, WE);
  Register #(.width(10)) register_1 (.D(Write_Data), .en(and_1_out), .Q(register_1_q), .clk(in_5));  // open: clr
  Register #(.width(10)) register_2 (.D(Write_Data), .en(and_2_out), .Q(register_2_q), .clk(in_5));  // open: clr
  Register #(.width(10)) register_3 (.D(Write_Data), .en(and_3_out), .Q(register_3_q), .clk(in_5));  // open: clr
  Register #(.width(10)) register_4 (.D(Write_Data), .en(and_4_out), .Q(register_4_q), .clk(in_5));  // open: clr
  Multiplexer #(.select(2), .width(10), .enable("false")) multiplexer_1 (
    .in0(register_1_q), .in1(register_2_q), .in2(register_3_q), .in3(register_4_q), .out(Data_1), .sel(RS));
  Multiplexer #(.select(2), .width(10), .enable("false")) multiplexer_2 (
    .in0(register_1_q), .in1(register_2_q), .in2(register_3_q), .in3(register_4_q), .out(Data_2), .sel(RT));
endmodule

module _1_Bit_ALU (
  input  B,
  input  A,
  input  Cin,
  input  [1:0] alu_op,
  output out_5,
  output out_6
);

  wire adder_1_out, and_1_out, or_1_out, subtractor_1_out;

  and and_1 (and_1_out, A, B);
  or or_1 (or_1_out, A, B);
  Adder #(.width(1)) adder_1 (.a(A), .b(B), .out(adder_1_out), .cin(Cin), .cout(out_6));
  Subtractor #(.width(1)) subtractor_1 (.a(A), .b(B), .out(subtractor_1_out));  // open: bin, bout
  Multiplexer #(.select(2), .enable("false")) multiplexer_1 (
    .in0(and_1_out), .in1(or_1_out), .in2(adder_1_out), .in3(subtractor_1_out), .out(out_5), .sel(alu_op));
endmodule

module _10_bit_ALU (
  input  [1:0] ALU_OP,
  input  [9:0] A,
  input  C_in,
  input  [9:0] B,
  output [9:0] ALU_out,
  output Zero,
  output OverFlow,
  output Cout
);

  wire n1_bit_alu_1_out_6, n1_bit_alu_2_out_6, n1_bit_alu_3_out_6, n1_bit_alu_4_out_6, n1_bit_alu_5_out_6,
       n1_bit_alu_6_out_6, n1_bit_alu_7_out_6, n1_bit_alu_8_out_6, n1_bit_alu_9_out_6;

  _1_Bit_ALU u_1_bit_alu_1 (
    .alu_op(ALU_OP), .out_5(ALU_out[0]), .out_6(n1_bit_alu_1_out_6), .B(B[0]), .A(A[0]), .Cin(C_in));
  _1_Bit_ALU u_1_bit_alu_2 (
    .alu_op(ALU_OP), .out_5(ALU_out[1]), .out_6(n1_bit_alu_2_out_6), .B(B[1]), .A(A[1]),
    .Cin(n1_bit_alu_1_out_6));
  _1_Bit_ALU u_1_bit_alu_3 (
    .alu_op(ALU_OP), .out_5(ALU_out[2]), .out_6(n1_bit_alu_3_out_6), .B(B[2]), .A(A[2]),
    .Cin(n1_bit_alu_2_out_6));
  _1_Bit_ALU u_1_bit_alu_4 (
    .alu_op(ALU_OP), .out_5(ALU_out[3]), .out_6(n1_bit_alu_4_out_6), .B(B[3]), .A(A[3]),
    .Cin(n1_bit_alu_3_out_6));
  _1_Bit_ALU u_1_bit_alu_5 (
    .alu_op(ALU_OP), .out_5(ALU_out[4]), .out_6(n1_bit_alu_5_out_6), .B(B[4]), .A(A[4]),
    .Cin(n1_bit_alu_4_out_6));
  _1_Bit_ALU u_1_bit_alu_6 (
    .alu_op(ALU_OP), .out_5(ALU_out[5]), .out_6(n1_bit_alu_6_out_6), .B(B[5]), .A(A[5]),
    .Cin(n1_bit_alu_5_out_6));
  _1_Bit_ALU u_1_bit_alu_7 (
    .alu_op(ALU_OP), .out_5(ALU_out[6]), .out_6(n1_bit_alu_7_out_6), .B(B[6]), .A(A[6]),
    .Cin(n1_bit_alu_6_out_6));
  _1_Bit_ALU u_1_bit_alu_8 (
    .alu_op(ALU_OP), .out_5(ALU_out[7]), .out_6(n1_bit_alu_8_out_6), .B(B[7]), .A(A[7]),
    .Cin(n1_bit_alu_7_out_6));
  _1_Bit_ALU u_1_bit_alu_9 (
    .alu_op(ALU_OP), .out_5(ALU_out[8]), .out_6(n1_bit_alu_9_out_6), .B(B[8]), .A(A[8]),
    .Cin(n1_bit_alu_8_out_6));
  _1_Bit_ALU u_1_bit_alu_10 (
    .alu_op(ALU_OP), .out_5(ALU_out[9]), .out_6(Cout), .B(B[9]), .A(A[9]), .Cin(n1_bit_alu_9_out_6));
  nor nor_1 (Zero, ALU_out[0], ALU_out[1], ALU_out[2], ALU_out[3], ALU_out[4], ALU_out[5], ALU_out[6], ALU_out[7], ALU_out[8], ALU_out[9]);
  or or_1 (OverFlow, n1_bit_alu_9_out_6, Cout);
endmodule

module R_Type (
  input  in_1,
  input  in_2,
  input  [1:0] ALU_OP,
  output [3:0] out_4,
  output [9:0] out_5,
  output [9:0] out_6,
  output out_7,
  output out_8,
  output out_9,
  output [9:0] out_10
);

  wire clock_1_out;
  wire [5:0] ram_1_data;
  wire [9:0] adder_1_out, register_1_q;

  Clock clock_1 (.out(clock_1_out));
  Adder #(.width(10)) adder_1 (.a(register_1_q), .b(10'h1), .out(adder_1_out));  // open: cin, cout
  Register #(.width(10)) register_1 (.D(adder_1_out), .Q(register_1_q), .clk(clock_1_out));  // open: en, clr
  RAM #(.addrWidth(10), .dataWidth(10)) ram_1 (
    .addr(register_1_q), .data({out_4, ram_1_data}), .clk(clock_1_out));  // open: sel, ld, clr
  _10_bit_Register_File u_10_bit_register_file_1 (
    .WE(in_2), .in_5(clock_1_out), .Data_1(out_5), .RS(ram_1_data[5:4]), .Data_2(out_10),
    .RT(ram_1_data[3:2]), .Write_Data(out_6), .RD(ram_1_data[1:0]));
  _10_bit_ALU u_10_bit_alu_1 (
    .A(out_5), .B(out_10), .ALU_out(out_6), .Zero(out_7), .OverFlow(out_8), .Cout(out_9), .ALU_OP(ALU_OP),
    .C_in(in_1));
endmodule

module I_Type (
  input  in_1,
  input  clear,
  input  mem_read,
  input  mem_write,
  input  in_5,
  input  clolck,
  output [9:0] out_7,
  output [9:0] out_8,
  output [9:0] out_9,
  output [9:0] out_10,
  output out_11,
  output out_12,
  output out_13,
  output [9:0] out_14,
  output [9:0] out_15
);

  wire [1:0] bit_extender_2_out;
  wire [9:0] adder_1_out, register_1_q;

  Register #(.width(10)) register_1 (.D(adder_1_out), .Q(register_1_q), .clk(clolck), .clr(clear));  // open: en
  Adder #(.width(10)) adder_1 (.a(register_1_q), .b(10'h1), .out(adder_1_out));  // open: cin, cout
  ROM #(.addrWidth(10), .dataWidth(10)) rom_1 (.addr(register_1_q), .data(out_8));  // open: sel
  _10_bit_Register_File u_10_bit_register_file_1 (
    .WE(in_5), .in_5(clolck), .Data_1(out_7), .RS(out_8[7:6]), .Data_2(out_14), .RT(out_8[5:4]),
    .Write_Data(out_10), .RD(out_8[5:4]));
  assign out_15 = {{6{1'b0}}, out_8[3:0]};  // Bit_Extender bit_extender_1
  _10_bit_ALU u_10_bit_alu_1 (
    .A(out_7), .B(out_15), .ALU_out(out_9), .Zero(out_11), .OverFlow(out_12), .Cout(out_13),
    .ALU_OP(out_8[9:8]), .C_in(in_1));
  Bit_Extender #(.in_width(10), .out_width(2)) bit_extender_2 (.in(out_9), .out(bit_extender_2_out));
  RAM #(.addrWidth(2), .dataWidth(10), .bus("separate")) ram_1 (
    .addr(bit_extender_2_out), .din(out_14), .data(out_10), .str(mem_read), .clk(clolck), .ld(mem_write));  // open: sel, clr

  // Notes on the sheet:
  //   contents of rom_1 (hex, n*v repeats v):
  //   61 60
endmodule

module Instruction_Fetch (
  input  clear,
  output [9:0] out_2
);

  wire clock_1_out;
  wire [9:0] adder_1_out, register_1_q;

  Clock clock_1 (.out(clock_1_out));
  Register #(.width(10)) register_1 (.D(adder_1_out), .Q(register_1_q), .clk(clock_1_out), .clr(clear));  // open: en
  Adder #(.width(10)) adder_1 (.a(register_1_q), .b(10'h1), .out(adder_1_out));  // open: cin, cout
  ROM #(.addrWidth(10), .dataWidth(10)) rom_1 (.addr(register_1_q), .data(out_2));  // open: sel

  // Notes on the sheet:
  //   contents of rom_1 (hex, n*v repeats v):
  //   5f 4e 11
endmodule
